# Fritzing sketch cbr-wiring (saved by Fritzing 0.9.3b)

parts:
  C1-M = Molex Picoblade Series Header [part_number=0533980871 package=Picoblade-53398-0871]
  C1-F = Molex Picoblade Series Header [part_number=0533980871 package=Picoblade-53398-0871]
  ECU-OBD = Molex Picoblade Series Header [part_number=0533980371 package=Picoblade-53398-0371]
  C3-F/M? = Molex Picoblade Series Header [part_number=0533980871 package=Picoblade-53398-0871]
  BAT-FUSE = DC Power [voltage=12V]  # not connected

nets:
  N1: C1-M.1, C1-F.1, ECU-OBD.1
  GND: C1-M.2, C1-F.2, ECU-OBD.2
  N2: C1-M.3, C1-F.3, ECU-OBD.3
  N3: C1-M.4, C1-F.4, C3-F/M?.2, C3-F/M?.3, C3-F/M?.4
  N4: C1-M.5, C1-F.5, C3-F/M?.5
  N5: C1-M.6, C1-F.6, C3-F/M?.6
  N6: C1-M.7, C1-F.7, C3-F/M?.7
  N7: C1-M.8, C1-F.8, C3-F/M?.8

notes:
  ECU K-LINE
  ECU 12V
  GND
  PWR 12V
  BAT 12V
  CAN_H
  CAN_L
